// Logisim project final_ckt.circ as structural Verilog: 3 circuits, main circuit can_tx
module can_tx (
  input  CLK,
  input  [10:0] in_2,
  input  IDE,
  input  START,
  input  OUT,
  input  [7:0] DATA,
  input  [3:0] DLC
);

  wire counter_1_carry, counter_2_carry, nor_1_out, not_1_out, not_2_out, not_3_out, not_4_out, not_5_out,
       not_6_out, shift_register_1_out, shift_register_2_out, shift_register_3_out;

  not not_1 (not_1_out, START);
  Counter #(.width(4), .max('h8), .ongoal("stay")) counter_1 (
    .load(not_1_out), .D(DLC), .count(START), .carry(counter_1_carry), .clk(counter_2_carry), .clr(START));  // open: Q
  Shift_Register #(.length(4)) shift_register_1 (
    .shift(START), .in(shift_register_3_out), .clk(CLK), .out(shift_register_1_out), .load(START), .d2(IDE));  // open: clr, d0, q0, d1, q1, q2, d3, q3
  Counter #(.width(4), .max('h8), .ongoal("stay")) counter_2 (
    .count(nor_1_out), .carry(counter_2_carry), .clk(CLK), .clr(START));  // open: load, D, Q
  nor nor_1 (nor_1_out, counter_1_carry, not_3_out);
  not not_2 (not_2_out, counter_2_carry);
  Shift_Register shift_register_2 (
    .shift(not_2_out), .clk(CLK), .out(shift_register_2_out), .load(counter_2_carry), .d0(DATA[7]),
    .d1(DATA[6]), .d2(DATA[5]), .d3(DATA[4]), .d4(DATA[3]), .d5(DATA[2]), .d6(DATA[1]), .d7(DATA[0]));  // open: in, clr, q0, q1, q2, q3, q4, q5, q6, q7
  not not_3 (not_3_out, START);
  not not_4 (not_4_out, START);
  Shift_Register #(.length(4)) shift_register_3 (
    .shift(START), .in(shift_register_2_out), .clk(CLK), .out(shift_register_3_out), .load(not_4_out),
    .d0(DLC[3]), .d1(DLC[2]), .d2(DLC[1]), .d3(DLC[0]));  // open: clr, q0, q1, q2, q3
  not not_5 (not_5_out, not_3_out);
  Shift_Register #(.length(12)) shift_register_4 (
    .shift(not_5_out), .in(shift_register_1_out), .clk(CLK), .out(OUT), .load(not_3_out), .d0(in_2[10]),
    .d1(in_2[9]), .d2(in_2[8]), .d3(in_2[7]), .d4(in_2[6]), .d5(in_2[5]), .d6(in_2[4]), .d7(in_2[3]),
    .d8(in_2[2]), .d9(in_2[1]), .d10(in_2[0]), .d11(not_6_out));  // open: clr, q0, q1, q2, q3, q4, q5, q6, q7, q8, q9, q10, q11
  not not_6 (not_6_out, not_3_out);

  // Other names for the same wires on the sheet: RST = START
endmodule

module can_rx (
  input  [10:0] ID11,
  input  IN,
  input  RST,
  input  [17:0] ID18,
  input  CLK,
  input  [7:0] D0,
  input  [7:0] D1,
  input  [7:0] D2,
  input  [7:0] D3,
  input  [7:0] D4,
  input  [7:0] D5,
  input  [7:0] D6,
  input  [7:0] D7
);

  wire and_1_out, and_2_out, and_3_out, and_4_out, and_5_out, comparator_1_eq, comparator_2_eq,
       counter_1_carry, counter_2_carry, counter_3_carry, counter_4_carry, demultiplexer_1_out0,
       demultiplexer_1_out1, IDE, not_1_out, not_2_out, not_3_out, not_4_out, or_1_out, or_2_out,
       shift_register_1_out, shift_register_2_out, shift_register_3_out, shift_register_5_out,
       shift_register_7_out, shift_register_8_q0, shift_register_9_out, shift_register_10_out,
       shift_register_11_out;
  wire [3:0] shift_register_4_q3;
  wire [10:0] shift_register_3_q12;
  wire [17:0] shift_register_6_q20;

  Counter #(.width(5), .max('h19), .ongoal("stay")) counter_1 (
    .count(not_4_out), .carry(counter_1_carry), .clk(CLK), .clr(RST));  // open: load, D, Q
  not not_1 (not_1_out, counter_1_carry);
  Shift_Register shift_register_1 (
    .shift(counter_3_carry), .in(and_5_out), .clk(CLK), .out(shift_register_1_out), .load(RST), .d0(RST),
    .q0(D0[7]), .d1(RST), .q1(D0[6]), .d2(RST), .q2(D0[5]), .d3(RST), .q3(D0[4]), .d4(RST), .q4(D0[3]),
    .d5(RST), .q5(D0[2]), .d6(RST), .q6(D0[1]), .d7(RST), .q7(D0[0]));  // open: clr
  not not_2 (not_2_out, IDE);
  not not_3 (not_3_out, counter_2_carry);
  Shift_Register shift_register_2 (
    .shift(counter_3_carry), .in(shift_register_1_out), .clk(CLK), .out(shift_register_2_out), .load(RST),
    .d0(RST), .q0(D1[7]), .d1(RST), .q1(D1[6]), .d2(RST), .q2(D1[5]), .d3(RST), .q3(D1[4]), .d4(RST),
    .q4(D1[3]), .d5(RST), .q5(D1[2]), .d6(RST), .q6(D1[1]), .d7(RST), .q7(D1[0]));  // open: clr
  and and_1 (and_1_out, not_4_out, comparator_1_eq);
  Demultiplexer demultiplexer_1 (
    .out0(demultiplexer_1_out0), .out1(demultiplexer_1_out1), .in(IN), .sel(and_1_out));  // open: en
  and and_2 (and_2_out, not_1_out, IDE);
  and and_3 (and_3_out, not_2_out, not_4_out);
  or or_1 (or_1_out, and_3_out, and_4_out);
  and and_4 (and_4_out, counter_1_carry, not_3_out);
  Shift_Register #(.length(13)) shift_register_3 (
    .shift(shift_register_8_q0), .in(demultiplexer_1_out0), .clk(CLK), .out(shift_register_3_out),
    .load(RST), .d0(RST), .q0(IDE), .d1(RST), .d2(RST), .q2(shift_register_3_q12[10]), .d3(RST),
    .q3(shift_register_3_q12[9]), .d4(RST), .q4(shift_register_3_q12[8]), .d5(RST),
    .q5(shift_register_3_q12[7]), .d6(RST), .q6(shift_register_3_q12[6]), .d7(RST),
    .q7(shift_register_3_q12[5]), .d8(RST), .q8(shift_register_3_q12[4]), .d9(RST),
    .q9(shift_register_3_q12[3]), .d10(RST), .q10(shift_register_3_q12[2]), .d11(RST),
    .q11(shift_register_3_q12[1]), .d12(RST), .q12(shift_register_3_q12[0]));  // open: clr, q1
  and and_5 (and_5_out, demultiplexer_1_out1, comparator_2_eq);
  Shift_Register #(.length(4)) shift_register_4 (
    .shift(or_1_out), .in(and_5_out), .clk(CLK), .load(RST), .d0(RST), .q0(shift_register_4_q3[3]), .d1(RST),
    .q1(shift_register_4_q3[2]), .d2(RST), .q2(shift_register_4_q3[1]), .d3(RST), .q3(shift_register_4_q3[0]));  // open: out, clr
  Shift_Register shift_register_5 (
    .shift(counter_3_carry), .in(shift_register_2_out), .clk(CLK), .out(shift_register_5_out), .load(RST),
    .d0(RST), .q0(D2[7]), .d1(RST), .q1(D2[6]), .d2(RST), .q2(D2[5]), .d3(RST), .q3(D2[4]), .d4(RST),
    .q4(D2[3]), .d5(RST), .q5(D2[2]), .d6(RST), .q6(D2[1]), .d7(RST), .q7(D2[0]));  // open: clr
  Comparator #(.width(11)) comparator_1 (.a(ID11), .b(shift_register_3_q12), .eq(comparator_1_eq));  // open: gt, lt
  Shift_Register #(.length(21)) shift_register_6 (
    .shift(and_2_out), .in(and_5_out), .clk(CLK), .load(RST), .d0(RST), .d1(RST), .d2(RST), .d3(RST),
    .q3(shift_register_6_q20[17]), .d4(RST), .q4(shift_register_6_q20[16]), .d5(RST),
    .q5(shift_register_6_q20[15]), .d6(RST), .q6(shift_register_6_q20[14]), .d7(RST),
    .q7(shift_register_6_q20[13]), .d8(RST), .q8(shift_register_6_q20[12]), .d9(RST),
    .q9(shift_register_6_q20[11]), .d10(RST), .q10(shift_register_6_q20[10]), .d11(RST),
    .q11(shift_register_6_q20[9]), .d12(RST), .q12(shift_register_6_q20[8]), .d13(RST),
    .q13(shift_register_6_q20[7]), .d14(RST), .q14(shift_register_6_q20[6]), .d15(RST),
    .q15(shift_register_6_q20[5]), .d16(RST), .q16(shift_register_6_q20[4]), .d17(RST),
    .q17(shift_register_6_q20[3]), .d18(RST), .q18(shift_register_6_q20[2]), .d19(RST),
    .q19(shift_register_6_q20[1]), .d20(RST), .q20(shift_register_6_q20[0]));  // open: out, clr, q0, q1, q2
  Counter #(.width(2), .max('h0), .ongoal("stay")) counter_2 (
    .count(or_1_out), .carry(counter_2_carry), .clk(CLK), .clr(RST));  // open: load, D, Q
  Shift_Register shift_register_7 (
    .shift(counter_3_carry), .in(shift_register_5_out), .clk(CLK), .out(shift_register_7_out), .load(RST),
    .d0(RST), .q0(D3[7]), .d1(RST), .q1(D3[6]), .d2(RST), .q2(D3[5]), .d3(RST), .q3(D3[4]), .d4(RST),
    .q4(D3[3]), .d5(RST), .q5(D3[2]), .d6(RST), .q6(D3[1]), .d7(RST), .q7(D3[0]));  // open: clr
  Shift_Register #(.length(1)) shift_register_8 (
    .shift(shift_register_8_q0), .in(shift_register_3_out), .clk(CLK), .load(RST), .d0(RST),
    .q0(shift_register_8_q0));  // open: out, clr
  Counter #(.width(4), .max('h9), .ongoal("stay")) counter_3 (
    .load(counter_2_carry), .D(shift_register_4_q3), .carry(counter_3_carry), .clk(CLK), .clr(or_2_out));  // open: count, Q
  or or_2 (or_2_out, RST, counter_4_carry);
  not not_4 (not_4_out, shift_register_8_q0);
  Counter #(.width(4), .max('h8), .ongoal("stay")) counter_4 (
    .count(counter_3_carry), .carry(counter_4_carry), .clk(CLK), .clr(RST));  // open: load, D, Q
  Shift_Register shift_register_9 (
    .shift(counter_3_carry), .in(shift_register_7_out), .clk(CLK), .out(shift_register_9_out), .load(RST),
    .d0(RST), .q0(D4[7]), .d1(RST), .q1(D4[6]), .d2(RST), .q2(D4[5]), .d3(RST), .q3(D4[4]), .d4(RST),
    .q4(D4[3]), .d5(RST), .q5(D4[2]), .d6(RST), .q6(D4[1]), .d7(RST), .q7(D4[0]));  // open: clr
  Comparator #(.width(18)) comparator_2 (.a(ID18), .b(shift_register_6_q20), .eq(comparator_2_eq));  // open: gt, lt
  Shift_Register shift_register_10 (
    .shift(counter_3_carry), .in(shift_register_9_out), .clk(CLK), .out(shift_register_10_out), .load(RST),
    .d0(RST), .q0(D5[7]), .d1(RST), .q1(D5[6]), .d2(RST), .q2(D5[5]), .d3(RST), .q3(D5[4]), .d4(RST),
    .q4(D5[3]), .d5(RST), .q5(D5[2]), .d6(RST), .q6(D5[1]), .d7(RST), .q7(D5[0]));  // open: clr
  Shift_Register shift_register_11 (
    .shift(counter_3_carry), .in(shift_register_10_out), .clk(CLK), .out(shift_register_11_out), .load(RST),
    .d0(RST), .q0(D6[7]), .d1(RST), .q1(D6[6]), .d2(RST), .q2(D6[5]), .d3(RST), .q3(D6[4]), .d4(RST),
    .q4(D6[3]), .d5(RST), .q5(D6[2]), .d6(RST), .q6(D6[1]), .d7(RST), .q7(D6[0]));  // open: clr
  Shift_Register shift_register_12 (
    .shift(counter_3_carry), .in(shift_register_11_out), .clk(CLK), .load(RST), .d0(RST), .q0(D7[7]),
    .d1(RST), .q1(D7[6]), .d2(RST), .q2(D7[5]), .d3(RST), .q3(D7[4]), .d4(RST), .q4(D7[3]), .d5(RST),
    .q5(D7[2]), .d6(RST), .q6(D7[1]), .d7(RST), .q7(D7[0]));  // open: out, clr

  // Notes on the sheet:
  //   ROM for storing CAN identifier of each device
  //   11 bit identifier+SRR+IDE
  //   ROM for ectended identifier
  //   Remaining 18 bits of identifier for extended version+RTR+2 reserved bits
  //   DATA (8 bytes)
endmodule

module main (
  input  in_1,
  input  [10:0] in_2,
  input  in_3,
  input  [7:0] in_4,
  input  in_5,
  input  [3:0] in_6,
  input  in_7,
  input  in_8,
  input  in_9,
  input  [17:0] TX,
  input  [31:0] in_11,
  input  [31:0] in_12
);

  can_tx can_tx_1 (.CLK(in_1), .in_2(in_2), .START(in_3), .OUT(in_5), .DATA(in_4), .DLC(in_6), .IDE(in_7));
  can_rx can_rx_1 (
    .IN(in_8), .RST(in_9), .ID11(in_2), .ID18(TX), .D0(in_11[7:0]), .D1(in_11[15:8]), .D2(in_11[23:16]),
    .D3(in_11[31:24]), .D4(in_12[7:0]), .D5(in_12[15:8]), .D6(in_12[23:16]), .D7(in_12[31:24]), .CLK(in_1));

  // Other names for the same wires on the sheet: CLK = in_1
endmodule
