// Logisim project hackathon (2).circ as structural Verilog: 1 circuit, main circuit main
module main (
  input  in_1,
  input  in_2
);

  wire and_1_out, and_2_out, and_3_out, and_4_out, CLK, comparator_1_eq, counter_1_carry, counter_2_carry,
       counter_3_carry, counter_4_carry, demultiplexer_1_out0, demultiplexer_1_out1, IDE, not_1_out,
       not_2_out, not_3_out, not_4_out, or_1_out, or_2_out, shift_register_1_out, shift_register_2_out,
       shift_register_4_out, shift_register_7_out, shift_register_8_out, shift_register_9_q0,
       shift_register_10_out, shift_register_11_out, shift_register_12_out;
  wire [3:0] shift_register_6_q3;
  wire [10:0] shift_register_3_q10, shift_register_4_q12;

  Clock clock_1 (.out(CLK));
  Counter #(.width(5), .max('h19), .ongoal("stay")) counter_1 (
    .count(not_4_out), .carry(counter_1_carry), .clk(CLK), .clr(in_2));  // open: load, D, Q
  Shift_Register shift_register_1 (
    .shift(counter_3_carry), .in(demultiplexer_1_out1), .clk(CLK), .out(shift_register_1_out), .load(in_2),
    .d0(in_2), .d1(in_2), .d2(in_2), .d3(in_2), .d4(in_2), .d5(in_2), .d6(in_2), .d7(in_2));  // open: clr, q0, q1, q2, q3, q4, q5, q6, q7
  not not_1 (not_1_out, counter_1_carry);
  not not_2 (not_2_out, IDE);
  not not_3 (not_3_out, counter_2_carry);
  Shift_Register shift_register_2 (
    .shift(counter_3_carry), .in(shift_register_1_out), .clk(CLK), .out(shift_register_2_out), .load(in_2),
    .d0(in_2), .d1(in_2), .d2(in_2), .d3(in_2), .d4(in_2), .d5(in_2), .d6(in_2), .d7(in_2));  // open: clr, q0, q1, q2, q3, q4, q5, q6, q7
  and and_1 (and_1_out, not_4_out, comparator_1_eq);
  Demultiplexer demultiplexer_1 (
    .out0(demultiplexer_1_out0), .out1(demultiplexer_1_out1), .in(in_1), .sel(and_1_out));  // open: en
  and and_2 (and_2_out, not_1_out, IDE);
  and and_3 (and_3_out, not_2_out, not_4_out);
  or or_1 (or_1_out, and_3_out, and_4_out);
  and and_4 (and_4_out, counter_1_carry, not_3_out);
  Shift_Register #(.length(11)) shift_register_3 (
    .q0(shift_register_3_q10[10]), .q1(shift_register_3_q10[9]), .q2(shift_register_3_q10[8]),
    .q3(shift_register_3_q10[7]), .q4(shift_register_3_q10[6]), .q5(shift_register_3_q10[5]),
    .q6(shift_register_3_q10[4]), .q7(shift_register_3_q10[3]), .q8(shift_register_3_q10[2]),
    .q9(shift_register_3_q10[1]), .q10(shift_register_3_q10[0]));  // open: shift, in, clk, out, load, clr, d0, d1, d2, d3, d4, d5, d6, d7, d8, d9, d10
  Shift_Register #(.length(13)) shift_register_4 (
    .shift(shift_register_9_q0), .in(demultiplexer_1_out0), .clk(CLK), .out(shift_register_4_out),
    .load(in_2), .d0(in_2), .q0(IDE), .d1(in_2), .d2(in_2), .q2(shift_register_4_q12[10]), .d3(in_2),
    .q3(shift_register_4_q12[9]), .d4(in_2), .q4(shift_register_4_q12[8]), .d5(in_2),
    .q5(shift_register_4_q12[7]), .d6(in_2), .q6(shift_register_4_q12[6]), .d7(in_2),
    .q7(shift_register_4_q12[5]), .d8(in_2), .q8(shift_register_4_q12[4]), .d9(in_2),
    .q9(shift_register_4_q12[3]), .d10(in_2), .q10(shift_register_4_q12[2]), .d11(in_2),
    .q11(shift_register_4_q12[1]), .d12(in_2), .q12(shift_register_4_q12[0]));  // open: clr, q1
  Shift_Register #(.length(21)) shift_register_5 (
    .shift(and_2_out), .in(demultiplexer_1_out1), .clk(CLK), .load(in_2), .d0(in_2), .d1(in_2), .d2(in_2),
    .d3(in_2), .d4(in_2), .d5(in_2), .d6(in_2), .d7(in_2), .d8(in_2), .d9(in_2), .d10(in_2), .d11(in_2),
    .d12(in_2), .d13(in_2), .d14(in_2), .d15(in_2), .d16(in_2), .d17(in_2), .d18(in_2), .d19(in_2), .d20(in_2));  // open: out, clr, q0, q1, q2, q3, q4, q5, q6, q7, q8, q9, q10, q11, q12, q13, q14, q15, q16, q17, q18, q19, q20
  Shift_Register #(.length(4)) shift_register_6 (
    .shift(or_1_out), .in(demultiplexer_1_out1), .clk(CLK), .load(in_2), .d0(in_2),
    .q0(shift_register_6_q3[3]), .d1(in_2), .q1(shift_register_6_q3[2]), .d2(in_2),
    .q2(shift_register_6_q3[1]), .d3(in_2), .q3(shift_register_6_q3[0]));  // open: out, clr
  Shift_Register shift_register_7 (
    .shift(counter_3_carry), .in(shift_register_2_out), .clk(CLK), .out(shift_register_7_out), .load(in_2),
    .d0(in_2), .d1(in_2), .d2(in_2), .d3(in_2), .d4(in_2), .d5(in_2), .d6(in_2), .d7(in_2));  // open: clr, q0, q1, q2, q3, q4, q5, q6, q7
  Comparator #(.width(11)) comparator_1 (
    .a(shift_register_3_q10), .b(shift_register_4_q12), .eq(comparator_1_eq));  // open: gt, lt
  Counter #(.width(2), .max('h0), .ongoal("stay")) counter_2 (
    .count(or_1_out), .carry(counter_2_carry), .clk(CLK), .clr(in_2));  // open: load, D, Q
  Shift_Register shift_register_8 (
    .shift(counter_3_carry), .in(shift_register_7_out), .clk(CLK), .out(shift_register_8_out), .load(in_2),
    .d0(in_2), .d1(in_2), .d2(in_2), .d3(in_2), .d4(in_2), .d5(in_2), .d6(in_2), .d7(in_2));  // open: clr, q0, q1, q2, q3, q4, q5, q6, q7
  Shift_Register #(.length(1)) shift_register_9 (
    .shift(shift_register_9_q0), .in(shift_register_4_out), .clk(CLK), .load(in_2), .d0(in_2),
    .q0(shift_register_9_q0));  // open: out, clr
  Counter #(.width(4), .max('h9), .ongoal("stay")) counter_3 (
    .load(counter_2_carry), .D(shift_register_6_q3), .carry(counter_3_carry), .clk(CLK), .clr(or_2_out));  // open: count, Q
  or or_2 (or_2_out, in_2, counter_4_carry);
  Shift_Register shift_register_10 (
    .shift(counter_3_carry), .in(shift_register_8_out), .clk(CLK), .out(shift_register_10_out), .load(in_2),
    .d0(in_2), .d1(in_2), .d2(in_2), .d3(in_2), .d4(in_2), .d5(in_2), .d6(in_2), .d7(in_2));  // open: clr, q0, q1, q2, q3, q4, q5, q6, q7
  not not_4 (not_4_out, shift_register_9_q0);
  Counter #(.width(4), .max('h8), .ongoal("stay")) counter_4 (
    .count(counter_3_carry), .carry(counter_4_carry), .clk(CLK), .clr(in_2));  // open: load, D, Q
  Shift_Register shift_register_11 (
    .shift(counter_3_carry), .in(shift_register_10_out), .clk(CLK), .out(shift_register_11_out), .load(in_2),
    .d0(in_2), .d1(in_2), .d2(in_2), .d3(in_2), .d4(in_2), .d5(in_2), .d6(in_2), .d7(in_2));  // open: clr, q0, q1, q2, q3, q4, q5, q6, q7
  Shift_Register shift_register_12 (
    .shift(counter_3_carry), .in(shift_register_11_out), .clk(CLK), .out(shift_register_12_out), .load(in_2),
    .d0(in_2), .d1(in_2), .d2(in_2), .d3(in_2), .d4(in_2), .d5(in_2), .d6(in_2), .d7(in_2));  // open: clr, q0, q1, q2, q3, q4, q5, q6, q7
  Shift_Register shift_register_13 (
    .shift(counter_3_carry), .in(shift_register_12_out), .clk(CLK), .load(in_2), .d0(in_2), .d1(in_2),
    .d2(in_2), .d3(in_2), .d4(in_2), .d5(in_2), .d6(in_2), .d7(in_2));  // open: out, clr, q0, q1, q2, q3, q4, q5, q6, q7

  // Other names for the same wires on the sheet: RST = in_2

  // Notes on the sheet:
  //   ROM for storing CAN identifier of each device
  //   11 bit identifier+SRR+IDE
  //   Remaining 18 bits of identifier for extended version+RTR+2 reserved bits
  //   DATA (8 bytes)
  //   Not yet implemented for CRC and ACK
endmodule
