// Logisim project transmitterfinalllllllll.circ as structural Verilog: 2 circuits, main circuit main
module main (
  input  in_1,
  input  in_2,
  input  in_3
);

  wire clk, shift_register_1_out, shift_register_2_out, shift_register_3_out, shift_register_4_out,
       shift_register_5_out, shift_register_6_out, shift_register_6_q0, shift_register_6_q1,
       shift_register_6_q2, shift_register_6_q3, shift_register_6_q4, shift_register_6_q5,
       shift_register_6_q6, shift_register_6_q7, shift_register_6_q8, shift_register_6_q9,
       shift_register_6_q10, shift_register_7_out, shift_register_8_out, shift_register_9_out, undriven;

  Shift_Register #(.length(4)) shift_register_1 (
    .shift(in_3), .in(undriven), .clk(clk), .out(shift_register_1_out));  // open: load, clr, d0, q0, d1, q1, d2, q2, d3, q3
  Shift_Register shift_register_2 (
    .shift(in_3), .in(shift_register_1_out), .clk(clk), .out(shift_register_2_out));  // open: load, clr, d0, q0, d1, q1, d2, q2, d3, q3, d4, q4, d5, q5, d6, q6, d7, q7
  Shift_Register shift_register_3 (
    .shift(in_3), .in(shift_register_2_out), .clk(clk), .out(shift_register_3_out));  // open: load, clr, d0, q0, d1, q1, d2, q2, d3, q3, d4, q4, d5, q5, d6, q6, d7, q7
  Shift_Register #(.length(3)) shift_register_4 (
    .in(undriven), .out(shift_register_4_out));  // open: shift, clk, load, clr, d0, q0, d1, q1, d2, q2
  Shift_Register shift_register_5 (
    .shift(in_3), .in(shift_register_3_out), .clk(clk), .out(shift_register_5_out));  // open: load, clr, d0, q0, d1, q1, d2, q2, d3, q3, d4, q4, d5, q5, d6, q6, d7, q7
  Shift_Register #(.length(11)) shift_register_6 (
    .out(shift_register_6_out), .q0(shift_register_6_q0), .q1(shift_register_6_q1), .q2(shift_register_6_q2),
    .q3(shift_register_6_q3), .q4(shift_register_6_q4), .q5(shift_register_6_q5), .q6(shift_register_6_q6),
    .q7(shift_register_6_q7), .q8(shift_register_6_q8), .q9(shift_register_6_q9), .q10(shift_register_6_q10));  // open: shift, in, clk, load, clr, d0, d1, d2, d3, d4, d5, d6, d7, d8, d9, d10
  Shift_Register #(.length(11)) shift_register_7 (
    .shift(in_2), .in(shift_register_4_out), .clk(clk), .out(shift_register_7_out), .load(in_1),
    .d0(shift_register_6_q0), .d1(shift_register_6_q1), .d2(shift_register_6_q2), .d3(shift_register_6_q3),
    .d4(shift_register_6_q4), .d5(shift_register_6_q5), .d6(shift_register_6_q6), .d7(shift_register_6_q7),
    .d8(shift_register_6_q8), .d9(shift_register_6_q9), .d10(shift_register_6_q10));  // open: clr, q0, q1, q2, q3, q4, q5, q6, q7, q8, q9, q10
  Shift_Register shift_register_8 (
    .shift(in_3), .in(shift_register_5_out), .clk(clk), .out(shift_register_8_out));  // open: load, clr, d0, q0, d1, q1, d2, q2, d3, q3, d4, q4, d5, q5, d6, q6, d7, q7
  Shift_Register shift_register_9 (
    .shift(in_3), .in(shift_register_8_out), .clk(clk), .out(shift_register_9_out));  // open: load, clr, d0, q0, d1, q1, d2, q2, d3, q3, d4, q4, d5, q5, d6, q6, d7, q7
  LED led_1 (.in(shift_register_6_out));
  Shift_Register shift_register_10 (
    .shift(in_3), .in(shift_register_9_out), .clk(clk));  // open: out, load, clr, d0, q0, d1, q1, d2, q2, d3, q3, d4, q4, d5, q5, d6, q6, d7, q7
  Clock clock_1 (.out(clk));
  LED led_2 (.in(shift_register_7_out));
endmodule

module rom (
  input  in_1,
  input  in_2,
  input  in_3,
  input  in_4
);

  wire clk, counter_2_carry, not_1_out, not_2_out, not_3_out, shift_register_1_out, shift_register_2_out,
       shift_register_3_out, shift_register_4_out;
  wire [5:0] counter_1_q;
  wire [7:0] rom_1_data;
  wire [10:0] rom_2_data;

  Counter #(.width(6), .max('h7)) counter_1 (
    .load(in_3), .count(in_4), .Q(counter_1_q), .clk(counter_2_carry));  // open: D, carry, clr
  Clock clock_1 (.out(clk));
  Shift_Register #(.length(3)) shift_register_1 (
    .in(shift_register_3_out), .clk(clk), .out(shift_register_1_out));  // open: shift, load, clr, d0, q0, d1, q1, d2, q2
  Counter #(.max('h8)) counter_2 (.count(in_4), .carry(counter_2_carry), .clk(clk));  // open: load, D, Q, clr
  ROM #(.addrWidth(6)) rom_1 (.addr(counter_1_q), .data(rom_1_data));  // open: sel
  not not_1 (not_1_out, counter_2_carry);
  Shift_Register shift_register_2 (
    .shift(not_1_out), .clk(clk), .out(shift_register_2_out), .load(counter_2_carry), .d0(rom_1_data[7]),
    .d1(rom_1_data[6]), .d2(rom_1_data[5]), .d3(rom_1_data[4]), .d4(rom_1_data[3]), .d5(rom_1_data[2]),
    .d6(rom_1_data[1]), .d7(rom_1_data[0]));  // open: in, clr, q0, q1, q2, q3, q4, q5, q6, q7
  Shift_Register #(.length(4)) shift_register_3 (
    .in(shift_register_2_out), .clk(clk), .out(shift_register_3_out));  // open: shift, load, clr, d0, q0, d1, q1, d2, q2, d3, q3
  ROM #(.addrWidth(2), .dataWidth(11)) rom_2 (.addr({2{in_1}}), .data(rom_2_data));  // open: sel
  not not_2 (not_2_out, in_2);
  Shift_Register #(.length(12)) shift_register_4 (
    .shift(not_2_out), .in(shift_register_1_out), .clk(clk), .out(shift_register_4_out), .load(in_2),
    .d0(rom_2_data[10]), .d1(rom_2_data[9]), .d2(rom_2_data[8]), .d3(rom_2_data[7]), .d4(rom_2_data[6]),
    .d5(rom_2_data[5]), .d6(rom_2_data[4]), .d7(rom_2_data[3]), .d8(rom_2_data[2]), .d9(rom_2_data[1]),
    .d10(rom_2_data[0]), .d11(not_3_out));  // open: clr, q0, q1, q2, q3, q4, q5, q6, q7, q8, q9, q10, q11
  not not_3 (not_3_out, in_2);

  // Notes on the sheet:
  //   contents of rom_1 (hex, n*v repeats v):
  //   6 72 87 34 23 65
  //   CAN BUS
  //   contents of rom_2 (hex, n*v repeats v):
  //   1ab
endmodule
